# Fritzing sketch Sketch (saved by Fritzing 0.9.10b)
breadboards: 1

parts:
  Mod1 = Meadow F7 Micro
  R1 = PHOTOCELL [package=photocell]
  R2 = Resistor [tolerance=±1% power=0.25 resistance=47 package=THT]

nets:
  N1: Mod1.3.3V, R1.P$1
  N2: Mod1.GND, R2.Pin_1
  N3: Mod1.A5, R1.P$2, R2.Pin_0
